# Fritzing sketch Schematic_P-I (saved by Fritzing 0.9.4)

parts:
  Part1 = Arduino Mega ADK (Rev3)
  U1 = ESP8266 WiFi Module [part_number=ESP8266]
  Rotary_Encoder1 = IDUINO Rotary Encoder SE055
  Display1 = LCD screen 16x2 IIC [part_number=101290]
  R2 = Resistor [tolerance=±5% resistance=220 package="0805 [SMD]"]
  R3 = Resistor [tolerance=±5% resistance=220 package="0805 [SMD]"]

nets:
  N1: Part1.D21/SCL, Display1.SCL
  N2: Part1.D20/SDA, Display1.SDA
  N3: Part1.D19/RX1, U1.TXD
  N4: Part1.D18/TX1, R3.Pin_0
  GND: Part1.GND, U1.GND, Rotary_Encoder1.GND, Display1.GND, R2.Pin_1
  3V3: Part1.3V3, U1.VCC
  5V: Part1.5V, Rotary_Encoder1.VDD, Display1.VCC
  N5: Part1.D4_PWM, Rotary_Encoder1.SW
  N6: Part1.D5_PWM, Rotary_Encoder1.CLK
  N7: Part1.D6_PWM, Rotary_Encoder1.DT
  N8: U1.RXD, R3.Pin_1

custom parts:
  ESP8266 WiFi Module: Generic WiFi Module based on the ESP8266 with onboard PCB antenna and UART communications
  IDUINO Rotary Encoder SE055: https://www.conrad.com/p/iduino-rotary-encoder-1-pcs-se055-1485328
  LCD screen 16x2 IIC: LCD screen with HD44780 controller enables showing text, symbols, value or anything else that comes from Croduino/Arduino. It is capable of showing 16 symbols in two lines and therefore can be used in many projects that need to send clearly visible and legible output information.. • Color of symbols: White • Backlight: Blue • Dimensions: 80 x 36 x 12 mm • Screen dimensions: 64.5 x 16 mm •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
